// Logisim project proyectoFinal.circ as structural Verilog: 1 circuit, main circuit main
module main (
  input  in_1,
  input  in_2,
  input  in_3,
  input  in_4,
  input  in_5,
  input  in_6,
  input  in_7,
  input  in_8,
  input  in_9,
  input  in_10,
  input  in_11,
  input  in_12,
  input  in_13,
  input  in_14,
  input  in_15,
  input  in_16,
  input  in_17,
  input  in_18,
  input  in_19,
  input  in_20,
  input  in_21
);

  wire button_1_out, e1, e2, e3, e4, e5, e6, e7, e8, e9, e10, e11, e12, e13, e14, e15, e16, e17, e18, e19,
       e20, e21, e22, e23, e24, e25, e26, e27, e28, e28s, e29, e29s, e30, e30s, e31, e31s, e32, mn, neg,
       not_3_out, not_4_out, not_5_out, not_6_out, not_7_out, not_8_out, not_9_out, not_10_out, not_11_out,
       not_12_out, not_13_out, not_14_out, not_15_out, rj, s1, s2, s3, s4, s5, s6, s7;
  wire [31:0] t3, t4, t5, t6, t7, t8, t9, t10, t11, t12, t13, t14, t15, t16;
  wire [31:30] t2;

  Clock clock_1 (.out(rj));
  not not_1 (mn, in_1);
  not not_2 (neg, in_2);
  Multiplexer #(.enable("false")) multiplexer_1 (.in0(in_16), .in1(neg), .out(t11[30]), .sel(s1));
  D_Flip_Flop d_ff_1 (.clk(rj), .D(e32), .Q(e1));  // open: Qn, preset, en, reset
  D_Flip_Flop d_ff_2 (.clk(rj), .D(e8), .Q(e9));  // open: Qn, preset, en, reset
  D_Flip_Flop d_ff_3 (.clk(rj), .D(e16), .Q(e17));  // open: Qn, preset, en, reset
  D_Flip_Flop d_ff_4 (.clk(rj), .D(e24), .Q(e25));  // open: Qn, preset, en, reset
  Multiplexer #(.enable("false")) multiplexer_2 (.in0(e28), .in1(neg), .out(e28s), .sel(not_3_out));
  not not_3 (not_3_out, s1);
  Multiplexer #(.enable("false")) multiplexer_3 (.in0(in_3), .in1(neg), .out(t2[30]), .sel(not_4_out));
  not not_4 (not_4_out, s2);
  D_Flip_Flop d_ff_5 (.clk(rj), .D(e1), .Q(e2));  // open: Qn, preset, en, reset
  D_Flip_Flop d_ff_6 (.clk(rj), .D(e9), .Q(e10));  // open: Qn, preset, en, reset
  D_Flip_Flop d_ff_7 (.clk(rj), .D(e17), .Q(e18));  // open: Qn, preset, en, reset
  D_Flip_Flop d_ff_8 (.clk(rj), .D(e25), .Q(e26));  // open: Qn, preset, en, reset
  Multiplexer #(.enable("false")) multiplexer_4 (.in0(e29), .in1(neg), .out(e29s), .sel(not_5_out));
  not not_5 (not_5_out, s1);
  Multiplexer #(.enable("false")) multiplexer_5 (.in0(in_4), .in1(neg), .out(t3[30]), .sel(not_6_out));
  not not_6 (not_6_out, s3);
  Multiplexer #(.enable("false")) multiplexer_6 (.in0(in_17), .in1(neg), .out(t12[30]), .sel(s2));
  D_Flip_Flop d_ff_9 (.clk(rj), .D(e2), .Q(e3));  // open: Qn, preset, en, reset
  D_Flip_Flop d_ff_10 (.clk(rj), .D(e10), .Q(e11));  // open: Qn, preset, en, reset
  D_Flip_Flop d_ff_11 (.clk(rj), .D(e18), .Q(e19));  // open: Qn, preset, en, reset
  D_Flip_Flop d_ff_12 (.clk(rj), .D(e26), .Q(e27));  // open: Qn, preset, en, reset
  Multiplexer #(.enable("false")) multiplexer_7 (.in0(in_5), .in1(neg), .out(t4[30]), .sel(not_7_out));
  not not_7 (not_7_out, s4);
  Multiplexer #(.enable("false")) multiplexer_8 (.in0(in_18), .in1(neg), .out(t13[30]), .sel(s3));
  D_Flip_Flop d_ff_13 (.clk(rj), .D(e3), .Q(e4));  // open: Qn, preset, en, reset
  D_Flip_Flop d_ff_14 (.clk(rj), .D(e11), .Q(e12));  // open: Qn, preset, en, reset
  D_Flip_Flop d_ff_15 (.clk(rj), .D(e19), .Q(e20));  // open: Qn, preset, en, reset
  D_Flip_Flop d_ff_16 (.clk(rj), .D(e27), .Q(e28));  // open: Qn, preset, en, reset
  Multiplexer #(.enable("false")) multiplexer_9 (.in0(e30), .in1(neg), .out(e30s), .sel(not_8_out));
  not not_8 (not_8_out, s1);
  Multiplexer #(.enable("false")) multiplexer_10 (.in0(in_6), .in1(neg), .out(t5[30]), .sel(not_9_out));
  not not_9 (not_9_out, s5);
  Multiplexer #(.enable("false")) multiplexer_11 (.in0(in_19), .in1(neg), .out(t14[30]), .sel(s4));
  D_Flip_Flop d_ff_17 (.clk(rj), .D(e4), .Q(e5));  // open: Qn, preset, en, reset
  D_Flip_Flop d_ff_18 (.clk(rj), .D(e12), .Q(e13));  // open: Qn, preset, en, reset
  D_Flip_Flop d_ff_19 (.clk(rj), .D(e20), .Q(e21));  // open: Qn, preset, en, reset
  D_Flip_Flop d_ff_20 (.clk(rj), .D(e28), .Q(e29));  // open: Qn, preset, en, reset
  Multiplexer #(.enable("false")) multiplexer_12 (.in0(e31), .in1(neg), .out(e31s), .sel(not_10_out));
  not not_10 (not_10_out, s1);
  Multiplexer #(.enable("false")) multiplexer_13 (.in0(in_7), .in1(neg), .out(t6[30]), .sel(not_11_out));
  not not_11 (not_11_out, s6);
  Multiplexer #(.enable("false")) multiplexer_14 (.in0(in_20), .in1(neg), .out(t15[30]), .sel(s5));
  D_Flip_Flop d_ff_21 (.clk(rj), .D(e5), .Q(e6));  // open: Qn, preset, en, reset
  D_Flip_Flop d_ff_22 (.clk(rj), .D(e13), .Q(e14));  // open: Qn, preset, en, reset
  D_Flip_Flop d_ff_23 (.clk(rj), .D(e21), .Q(e22));  // open: Qn, preset, en, reset
  D_Flip_Flop d_ff_24 (.clk(rj), .D(e29), .Q(e30));  // open: Qn, preset, en, reset
  Multiplexer #(.enable("false")) multiplexer_15 (.in0(in_8), .in1(neg), .out(t7[30]), .sel(not_12_out));
  not not_12 (not_12_out, in_12);
  Multiplexer #(.enable("false")) multiplexer_16 (.in0(in_21), .in1(neg), .out(t16[30]), .sel(s6));
  D_Flip_Flop d_ff_25 (.clk(rj), .D(e6), .Q(e7));  // open: Qn, preset, en, reset
  D_Flip_Flop d_ff_26 (.clk(rj), .D(e14), .Q(e15));  // open: Qn, preset, en, reset
  D_Flip_Flop d_ff_27 (.clk(rj), .D(e22), .Q(e23));  // open: Qn, preset, en, reset
  D_Flip_Flop d_ff_28 (.clk(rj), .D(e30), .Q(e31));  // open: Qn, preset, en, reset
  Multiplexer #(.enable("false")) multiplexer_17 (.in0(in_9), .in1(neg), .out(t8[30]), .sel(not_13_out));
  not not_13 (not_13_out, in_13);
  D_Flip_Flop d_ff_29 (.clk(rj), .D(e7), .Q(e8));  // open: Qn, preset, en, reset
  D_Flip_Flop d_ff_30 (.clk(rj), .D(e15), .Q(e16));  // open: Qn, preset, en, reset
  D_Flip_Flop d_ff_31 (.clk(rj), .D(e23), .Q(e24));  // open: Qn, preset, en, reset
  D_Flip_Flop d_ff_32 (.clk(rj), .D(e31), .Q(e32));  // open: Qn, preset, en, reset
  Multiplexer #(.enable("false")) multiplexer_18 (.in0(in_10), .in1(neg), .out(t9[30]), .sel(not_14_out));
  not not_14 (not_14_out, in_14);
  Multiplexer #(.enable("false")) multiplexer_19 (.in0(in_11), .in1(neg), .out(t10[30]), .sel(not_15_out));
  not not_15 (not_15_out, in_15);
  DotMatrix #(.inputtype("row"), .matrixcols(32), .matrixrows(16)) dotmatrix_1 (
    .row0({t16[31:30], {3{t16[30]}}, t16[26:0]}), .row1({t15[31:30], {3{t15[30]}}, t15[26:0]}),
    .row2({t14[31:30], {3{t14[30]}}, t14[26:0]}), .row3({t13[31:30], {3{t13[30]}}, t13[26:0]}),
    .row4({t12[31:30], {3{t12[30]}}, t12[26:0]}), .row5({t11[31:30], {3{t11[30]}}, t11[26:0]}),
    .row6({t10[31:30], {3{t10[30]}}, t10[26:0]}), .row7({t9[31:30], {3{t9[30]}}, t9[26:0]}),
    .row8({t8[31:30], {3{t8[30]}}, t8[26:0]}), .row9({t7[31:30], {3{t7[30]}}, t7[26:0]}),
    .row10({t6[31:30], {3{t6[30]}}, t6[26:0]}), .row11({t5[31:30], {3{t5[30]}}, t5[26:0]}),
    .row12({t4[31:30], {3{t4[30]}}, t4[26:0]}), .row13({t3[31:30], {3{t3[30]}}, t3[26:0]}),
    .row14({t2, {3{t2[30]}}, e27, e26, e25, e24, e23, e22, e21, e20, e19, e18, e17, e16, e15, e14, e13, e12, e11, e10, e9, e8, e7, e6, e5, e4, e3, e2, e1}),
    .row15({e32, e31s, e30s, e29s, e28s, e27, e26, e25, e24, e23, e22, e21, e20, e19, e18, e17, e16, e15, e14, e13, e12, e11, e10, e9, e8, e7, e6, e5, e4, e3, e2, e1}));
  D_Flip_Flop d_ff_33 (.clk(rj), .D(s1), .Q(s2), .reset(s7));  // open: Qn, preset, en
  D_Flip_Flop d_ff_34 (.clk(rj), .D(s2), .Q(s3), .reset(s7));  // open: Qn, preset, en
  D_Flip_Flop d_ff_35 (.clk(rj), .D(s3), .Q(s4), .reset(s7));  // open: Qn, preset, en
  D_Flip_Flop d_ff_36 (.clk(rj), .D(s4), .Q(s5), .reset(s7));  // open: Qn, preset, en
  D_Flip_Flop d_ff_37 (.clk(rj), .D(s5), .Q(s6), .reset(s7));  // open: Qn, preset, en
  D_Flip_Flop d_ff_38 (.clk(rj), .D(s6), .Q(s7));  // open: Qn, preset, en, reset
  Button button_1 (.out(button_1_out));
  D_Flip_Flop d_ff_39 (.clk(rj), .Q(s1), .preset(button_1_out), .reset(s7));  // open: D, Qn, en

  // Other names for the same wires on the sheet: t1[31:0] = {e32, e31s, e30s, e29s, e28s, e27, e26, e25, e24, e23, e22, e21, e20, e19, e18, e17, e16, e15, e14, e13, e12, e11, e10, e9, e8, e7, e6, e5, e4, e3, e2, e1};
  //   t2[29:0] = {{3{t2[30]}}, e27, e26, e25, e24, e23, e22, e21, e20, e19, e18, e17, e16, e15, e14, e13, e12, e11, e10, e9, e8, e7, e6, e5, e4, e3, e2, e1};
  //   t3[29:27] = {3{t3[30]}}; t4[29:27] = {3{t4[30]}}; t5[29:27] = {3{t5[30]}}; t6[29:27] = {3{t6[30]}};
  //   t7[29:27] = {3{t7[30]}}; t8[29:27] = {3{t8[30]}}; t9[29:27] = {3{t9[30]}}; t10[29:27] = {3{t10[30]}};
  //   t11[29:27] = {3{t11[30]}}; t12[29:27] = {3{t12[30]}}; t13[29:27] = {3{t13[30]}}; t14[29:27] = {3{t14[30]}};
  //   t15[29:27] = {3{t15[30]}}; t16[29:27] = {3{t16[30]}}

  // Notes on the sheet:
  //   jugador
  //   muñeco: 4x10
  //   obstaculo abajo: 2x5
  //   obstaculo arriba: 2x8
endmodule
